# Fritzing sketch Input - Distance (saved by Fritzing 0.9.1b)

parts:
  Part2 = SRF05 Ultrasonic Rangefinder
  Part3 = Arduino Uno (Rev3)

nets:
  VCC: Part2.VCC, Part3.5V
  N1: Part2.Trig, Part3.D13/SCK
  N2: Part2.Echo, Part3.D12/MISO
  GND: Part2.GND, Part3.GND
